# Fritzing sketch wearable_v0 (saved by Fritzing 1.0.7)
breadboards: 1

parts:
  Part1 = Arduino Nano (Rev3.0)
  HM-10_BLE = Bluetooth HM-10
  MAX30102 = MakerFocus MAX30102
  R1 = Resistor [tolerance=±5% power=0.25W resistance=2.2k package=THT]
  R2 = Resistor [tolerance=±5% power=0.25W resistance=1k package=THT]

nets:
  N1: Part1.D2, HM-10_BLE.TXD
  N2: Part1.D3, HM-10_BLE.RXD, R1.Pin_1, R2.Pin_0, R2.Pin_1
  GND: Part1.GND, HM-10_BLE.GND, MAX30102.GND, R1.Pin_0
  N3: Part1.A5, MAX30102.SCL
  N4: Part1.A4, MAX30102.SDA
  3V3: Part1.3V3, HM-10_BLE.VCC, MAX30102.VIN

notes:
  Vin
  GND
  SDA
  SCL

custom parts:
  MakerFocus MAX30102: Oximeter module using the MAX30102 chip. As usual, if you want the mounting holes in pcb, you need to drag a hole over the pad in silkscreen to actually drill the hole (by default they are not drilled)
